// Logisim project AND_.circ as structural Verilog: 1 circuit, main circuit AND_GATE
module AND_GATE (
  input  in_1,
  input  in_2,
  output out_3
);

  wire pull_resistor_1_node, transistor_2_out;

  Pull_Resistor #(.pull(1)) pull_resistor_1 (.node(pull_resistor_1_node));
  Transistor #(.\type ("n")) transistor_1 (.in(transistor_2_out), .out(pull_resistor_1_node), .gate(in_1));
  Transistor #(.\type ("n")) transistor_2 (.in(1'b0), .out(transistor_2_out), .gate(in_2));
  Pull_Resistor #(.pull(1)) pull_resistor_2 (.node(out_3));
  Transistor #(.\type ("n")) transistor_3 (.in(1'b0), .out(out_3), .gate(pull_resistor_1_node));
endmodule
