// Logisim project GATE.circ as structural Verilog: 9 circuits, main circuit HALF_ADDER
module NAND_GATE (
  input  in_1,
  input  in_2,
  output out_3
);

  wire transistor_2_out;

  Pull_Resistor #(.pull(1)) pull_resistor_1 (.node(out_3));
  Transistor #(.\type ("n")) transistor_1 (.in(transistor_2_out), .out(out_3), .gate(in_1));
  Transistor #(.\type ("n")) transistor_2 (.in(1'b0), .out(transistor_2_out), .gate(in_2));
endmodule

module AND_GATE (
  input  in_1,
  input  in_2,
  output out_3
);

  wire pull_resistor_1_node, transistor_2_out;

  Pull_Resistor #(.pull(1)) pull_resistor_1 (.node(pull_resistor_1_node));
  Transistor #(.\type ("n")) transistor_1 (.in(transistor_2_out), .out(pull_resistor_1_node), .gate(in_1));
  Transistor #(.\type ("n")) transistor_2 (.in(1'b0), .out(transistor_2_out), .gate(in_2));
  Pull_Resistor #(.pull(1)) pull_resistor_2 (.node(out_3));
  Transistor #(.\type ("n")) transistor_3 (.in(1'b0), .out(out_3), .gate(pull_resistor_1_node));
endmodule

module OR_GATE (
  input  in_1,
  input  in_2,
  output out_3
);

  wire transistor_1_out;

  Transistor #(.\type ("n")) transistor_1 (.in(1'b0), .out(transistor_1_out), .gate(in_1));
  Pull_Resistor #(.pull(1)) pull_resistor_1 (.node(transistor_1_out));
  Transistor #(.\type ("n")) transistor_2 (.in(1'b0), .out(transistor_1_out), .gate(in_2));
  Pull_Resistor #(.pull(1)) pull_resistor_2 (.node(out_3));
  Transistor #(.\type ("n")) transistor_3 (.in(1'b0), .out(out_3), .gate(transistor_1_out));
endmodule

module NOR_GATE (
  input  in_1,
  input  in_2,
  output out_3
);

  Transistor #(.\type ("n")) transistor_1 (.in(1'b0), .out(out_3), .gate(in_1));
  Pull_Resistor #(.pull(1)) pull_resistor_1 (.node(out_3));
  Transistor #(.\type ("n")) transistor_2 (.in(1'b0), .out(out_3), .gate(in_2));
endmodule

module NOT_GATE (
  input  in_1,
  output out_2
);

  Pull_Resistor #(.pull(1)) pull_resistor_1 (.node(out_2));
  Transistor #(.\type ("n")) transistor_1 (.in(1'b0), .out(out_2), .gate(in_1));
endmodule

module XOR_GATE (
  input  A,
  input  B,
  output out_3
);

  wire nand_gate_1_out_3, nand_gate_2_out_3, not_gate_1_out_2, not_gate_2_out_2;

  NOT_GATE not_gate_1 (.in_1(A), .out_2(not_gate_1_out_2));
  NOT_GATE not_gate_2 (.in_1(B), .out_2(not_gate_2_out_2));
  NAND_GATE nand_gate_1 (.in_1(not_gate_1_out_2), .in_2(not_gate_2_out_2), .out_3(nand_gate_1_out_3));
  NAND_GATE nand_gate_2 (.in_1(A), .in_2(B), .out_3(nand_gate_2_out_3));
  AND_GATE and_gate_1 (.in_1(nand_gate_1_out_3), .in_2(nand_gate_2_out_3), .out_3(out_3));
endmodule

module XNOR_GATE (
  input  in_1,
  input  in_2,
  output out_3
);

  wire and_gate_1_out_3, and_gate_2_out_3, not_gate_1_out_2, not_gate_2_out_2;

  NOT_GATE not_gate_1 (.in_1(in_1), .out_2(not_gate_1_out_2));
  NOT_GATE not_gate_2 (.in_1(in_2), .out_2(not_gate_2_out_2));
  AND_GATE and_gate_1 (.in_1(not_gate_1_out_2), .in_2(not_gate_2_out_2), .out_3(and_gate_1_out_3));
  AND_GATE and_gate_2 (.in_1(in_1), .in_2(in_2), .out_3(and_gate_2_out_3));
  OR_GATE or_gate_1 (.in_1(and_gate_1_out_3), .in_2(and_gate_2_out_3), .out_3(out_3));
endmodule

module HALF_ADDER (
  input  A,
  input  B,
  output out_3,
  output out_4
);

  xor xor_1 (out_3, A, B);
  and and_1 (out_4, B, A);
endmodule

module FULL_ADDER (
  input  in_1,
  input  in_2,
  input  in_3,
  output out_4,
  output out_5
);

  wire and_1_out, and_2_out, xor_1_out;

  xor xor_1 (xor_1_out, in_1, in_2);
  and and_1 (and_1_out, xor_1_out, in_3);
  and and_2 (and_2_out, in_2, in_1);
  xor xor_2 (out_4, xor_1_out, in_3);
  or or_1 (out_5, and_1_out, and_2_out);
endmodule
