// Logisim project NAND.circ as structural Verilog: 1 circuit, main circuit NAND_GATE
module NAND_GATE (
  input  in_1,
  input  in_2,
  output out_3
);

  wire transistor_2_out;

  Pull_Resistor #(.pull(1)) pull_resistor_1 (.node(out_3));
  Transistor #(.\type ("n")) transistor_1 (.in(transistor_2_out), .out(out_3), .gate(in_1));
  Transistor #(.\type ("n")) transistor_2 (.in(1'b0), .out(transistor_2_out), .gate(in_2));
endmodule
