// Logisim project NOR.circ as structural Verilog: 1 circuit, main circuit NOR_GATE
module NOR_GATE (
  input  in_1,
  input  in_2,
  output out_3
);

  wire transistor_2_out;

  Transistor #(.\type ("n")) transistor_1 (.in(transistor_2_out), .out(out_3), .gate(in_1));
  Pull_Resistor #(.pull(1)) pull_resistor_1 (.node(out_3));
  Transistor #(.\type ("n")) transistor_2 (.in(out_3), .out(transistor_2_out), .gate(in_2));
  // also tied to GND on the sheet: transistor_2_out
endmodule
