// Logisim project OR.circ as structural Verilog: 1 circuit, main circuit OR_GATE
module OR_GATE (
  input  in_1,
  input  in_2,
  output out_3
);

  wire pull_resistor_1_node;

  Pull_Resistor #(.pull(1)) pull_resistor_1 (.node(pull_resistor_1_node));
  Transistor #(.\type ("n")) transistor_1 (.in(1'b0), .out(pull_resistor_1_node), .gate(in_1));
  Transistor #(.\type ("n")) transistor_2 (.in(1'b0), .out(pull_resistor_1_node), .gate(in_2));
  Pull_Resistor #(.pull(1)) pull_resistor_2 (.node(out_3));
  Transistor #(.\type ("n")) transistor_3 (.in(1'b0), .out(out_3), .gate(pull_resistor_1_node));
endmodule
